# Fritzing sketch Seed_Germinator (saved by Fritzing 0.9.3b)
breadboards: 1

parts:
  U1 = NodeMCU V1.0
  Part1 = Soil Moisture Sensor
  RHT1 = Humidity and Temperature Sensor RHT03
  U2 = 2-Channel 5v Relay Shield [package=relay-2ch5v10a]

nets:
  N1: U1.D0, U2.IN1
  N2: U1.D1, U2.IN2
  N3: U1.D2, RHT1.Data-signal
  N4: U1.D3, U2.VCC
  GND: U1.GND, Part1.GND, RHT1.GND_2, U2.GND
  VCC: U1.Vin, Part1.VCC, RHT1.Vcc
  N5: U1.A0, Part1.SIG

notes:
  +5V
  0V
  +12V TO PUMP
  +12V SOURCE
  220V AC LIVE  SOURCE
  220V LIVE TO LAMP
  DHT22
  0v

custom parts:
  NodeMCU V1.0: ESP8266 based NodeMCU
  2-Channel 5v Relay Shield: 2 Channel 5v Relay Shield w. 2x SPD-06VDC-SD-C
